# Fritzing sketch MotoerController (saved by Fritzing 0.9.5d)
breadboards: 1

parts:
  Melikşah1 = Arduino Uno (Rev3)
  IC1 = L293D [package=THT]
  M1 = DC Motor
  S1 = Pushbutton [package="[THT]"]

nets:
  N1: Melikşah1.D11_PWM/MOSI, IC1.Enable_1
  N2: Melikşah1.D12/MISO, IC1.In_1
  N3: Melikşah1.D13/SCK, IC1.In_2
  N4: Melikşah1.GND, IC1.0V, S1.Pin_1, S1.Pin_2
  N5: Melikşah1.D2, S1.Pin_3, S1.Pin_4
  N6: Melikşah1.3V3, IC1.+Vmotor
  N7: Melikşah1.5V, IC1.+V
  N8: IC1.Out_1_(_Controlled_by_Enable_1_), M1.pin_2
  N9: IC1.Out_2_(_Controlled_by_Enable_1_), M1.pin_1
